// Logisim project Class_1.circ as structural Verilog: 1 circuit, main circuit main
module main (
  input  in_1,
  input  in_2,
  input  in_3,
  input  in_4,
  input  in_5,
  input  in_6,
  input  in_7,
  output out_8,
  output out_9
);

  wire and_1_out, nand_1_out, nand_2_out;

  nand nand_1 (nand_1_out, in_1, in_2);
  nand nand_2 (nand_2_out, in_3, in_4);
  and and_1 (and_1_out, in_5, in_6);
  nor nor_1 (out_9, and_1_out, in_7);
  xor xor_1 (out_8, nand_1_out, nand_2_out);
endmodule
