// Logisim project Class_2.circ as structural Verilog: 1 circuit, main circuit main
module main (
  input  in_1,
  input  in_2,
  input  in_3,
  input  in_4,
  input  in_5,
  input  in_6,
  input  in_7,
  input  in_8,
  input  in_9,
  input  in_10,
  output out_11,
  output out_12,
  output out_13,
  output out_14,
  output out_15,
  output out_16
);

  wire and_1_out, and_2_out, and_3_out, and_4_out, nand_2_out, nand_3_out, nor_2_out, nor_3_out, not_1_out,
       not_2_out, not_3_out, not_4_out;

  not not_1 (not_1_out, in_1);
  not not_2 (not_2_out, in_2);
  not not_3 (not_3_out, in_5);
  not not_4 (not_4_out, in_7);
  and and_1 (and_1_out, not_1_out, in_2);
  and and_2 (and_2_out, in_1, not_2_out);
  and and_3 (and_3_out, not_3_out, not_4_out);
  and and_4 (and_4_out, in_5, in_7);
  or or_1 (out_11, and_1_out, and_2_out);
  or or_2 (out_14, and_3_out, and_4_out);
  nand nand_1 (out_12, in_3, in_3);
  nor nor_1 (out_13, in_4, in_4);
  nand nand_2 (nand_2_out, in_6, in_6);
  nand nand_3 (nand_3_out, in_8, in_8);
  nor nor_2 (nor_2_out, in_9, in_9);
  nor nor_3 (nor_3_out, in_10, in_10);
  nand nand_4 (out_15, nand_2_out, nand_3_out);
  nor nor_4 (out_16, nor_2_out, nor_3_out);
endmodule
