// Logisim project Class_3.circ as structural Verilog: 2 circuits, main circuit main
module main (
  input  in_1,
  input  in_2,
  input  in_3,
  output out_4,
  output out_5
);

  wire and_1_out, and_2_out, xor_1_out, xor_3_out;

  xor xor_1 (xor_1_out, in_1, in_2);
  xor xor_2 (out_4, xor_1_out, in_3);
  and and_1 (and_1_out, in_2, in_3);
  xor xor_3 (xor_3_out, in_2, in_3);
  and and_2 (and_2_out, xor_3_out, in_1);
  or or_1 (out_5, and_1_out, and_2_out);
endmodule

module lalalala (
  input  in_1,
  input  in_2,
  input  in_3,
  output out_4,
  output out_5
);

  wire and_1_out, and_2_out, xor_1_out, xor_3_out;

  xor xor_1 (xor_1_out, in_1, in_2);
  xor xor_2 (out_4, xor_1_out, in_3);
  and and_1 (and_1_out, in_2, in_3);
  xor xor_3 (xor_3_out, in_2, in_3);
  and and_2 (and_2_out, xor_3_out, in_1);
  or or_1 (out_5, and_1_out, and_2_out);
endmodule
