// Logisim project Class_4.circ as structural Verilog: 2 circuits, main circuit main
module main (
  input  in_1,
  input  in_2,
  input  in_3,
  input  in_4,
  input  in_5,
  input  in_6,
  input  in_7,
  input  in_8
);

  wire adder_1_cout, adder_2_cout, adder_3_cout, not_1_out, not_2_out, not_3_out, not_4_out;
  wire [0:0] adder_4_cout;
  wire [3:0] adder_1_out, adder_5_out;

  Adder #(.width(1)) adder_1 (.a(in_1), .b(in_2), .out(adder_1_out[0]), .cin(1'b0), .cout(adder_1_cout));
  Adder #(.width(1)) adder_2 (.a(in_3), .b(in_4), .out(adder_1_out[1]), .cin(adder_1_cout), .cout(adder_2_cout));
  Adder #(.width(1)) adder_3 (.a(in_5), .b(in_6), .out(adder_1_out[2]), .cin(adder_2_cout), .cout(adder_3_cout));
  Adder #(.width(1)) adder_4 (.a(in_7), .b(in_8), .out(adder_1_out[3]), .cin(adder_3_cout), .cout(adder_4_cout[0]));
  not not_1 (not_1_out, in_2);
  not not_2 (not_2_out, in_4);
  not not_3 (not_3_out, in_6);
  not not_4 (not_4_out, in_8);
  Adder #(.width(1)) adder_5 (.a(not_1_out), .b(1'b1), .out(adder_5_out[0]), .cin(1'b0));  // open: cout
  Adder #(.width(1)) adder_6 (.a(not_2_out), .b(1'b0), .out(adder_5_out[1]));  // open: cin, cout
  Adder #(.width(1)) adder_7 (.a(not_3_out), .b(1'b0), .out(adder_5_out[2]));  // open: cin, cout
  Adder #(.width(1)) adder_8 (.a(not_4_out), .b(1'b0), .out(adder_5_out[3]));  // open: cin, cout
  Hex_Digit_Display hex_digit_display_1 (.value({3'b000, adder_4_cout[0]}));  // open: dp
  Hex_Digit_Display hex_digit_display_2 (.value(adder_1_out));  // open: dp
  Hex_Digit_Display hex_digit_display_3 (.value(adder_5_out));  // open: dp
endmodule

module lalalala (
  input  in_1,
  input  in_2,
  input  in_3,
  output out_4,
  output out_5
);

  wire and_1_out, and_2_out, xor_1_out, xor_3_out;

  xor xor_1 (xor_1_out, in_1, in_2);
  xor xor_2 (out_4, xor_1_out, in_3);
  and and_1 (and_1_out, in_2, in_3);
  xor xor_3 (xor_3_out, in_2, in_3);
  and and_2 (and_2_out, xor_3_out, in_1);
  or or_1 (out_5, and_1_out, and_2_out);
endmodule
