// Logisim project Class_5.circ as structural Verilog: 1 circuit, main circuit main
module main (
  input  in_1,
  input  in_2,
  input  in_3,
  input  in_4,
  input  in_5,
  input  in_6,
  input  in_7,
  input  in_8,
  input  in_9,
  input  in_10,
  input  in_11
);

  wire demultiplexer_1_out0, demultiplexer_1_out1;
  wire [3:0] multiplexer_1_out;

  Demultiplexer demultiplexer_1 (
    .out0(demultiplexer_1_out0), .out1(demultiplexer_1_out1), .in(in_10), .sel(in_11));  // open: en
  Multiplexer multiplexer_1 (.in0(in_2), .in1(in_3), .out(multiplexer_1_out[0]), .sel(in_1));  // open: en
  Multiplexer multiplexer_2 (.in0(in_4), .in1(in_5), .out(multiplexer_1_out[1]), .sel(in_1));  // open: en
  Multiplexer multiplexer_3 (.in0(in_6), .in1(in_7), .out(multiplexer_1_out[2]), .sel(in_1));  // open: en
  Multiplexer multiplexer_4 (.in0(in_8), .in1(in_9), .out(multiplexer_1_out[3]), .sel(in_1));  // open: en
  LED led_1 (.in(demultiplexer_1_out0));
  LED led_2 (.in(demultiplexer_1_out1));
  Hex_Digit_Display hex_digit_display_1 (.value(multiplexer_1_out));  // open: dp
endmodule
