// Logisim project Class_6.circ as structural Verilog: 1 circuit, main circuit main
module main (
  input  A,
  input  B,
  input  C,
  input  D,
  output E1,
  output E2
);

  wire and_1_out, and_2_out, and_3_out, not_1_out, not_2_out, not_3_out, not_4_out, not_5_out, not_6_out,
       not_7_out, or_1_out;

  not not_1 (not_1_out, A);
  not not_2 (not_2_out, B);
  not not_3 (not_3_out, C);
  not not_4 (not_4_out, D);
  not not_5 (not_5_out, B);
  not not_6 (not_6_out, C);
  and and_1 (and_1_out, not_3_out, not_4_out);
  not not_7 (not_7_out, A);
  and and_2 (and_2_out, B, not_7_out);
  and and_3 (and_3_out, A, not_5_out, not_6_out);
  or or_1 (or_1_out, not_2_out, and_1_out);
  or or_2 (E2, and_2_out, and_3_out);
  and and_4 (E1, not_1_out, or_1_out);
endmodule
