// Logisim project 10_08.circ as structural Verilog: 1 circuit, main circuit main
module main (
  input  in_1,
  input  in_2,
  input  in_3,
  input  in_4,
  input  in_5,
  input  in_6,
  input  in_7,
  input  in_8,
  input  in_9,
  input  in_10,
  input  in_11
);

  wire button_1_out;
  wire [3:0] shift_register_1_q3, shift_register_1_q7;

  Button button_1 (.out(button_1_out));
  Keyboard keyboard_1 ();  // open: clk, re, clr, avail, data
  Shift_Register shift_register_1 (
    .shift(in_10), .in(1'b0), .clk(button_1_out), .load(in_9), .clr(in_11), .d0(in_1),
    .q0(shift_register_1_q3[3]), .d1(in_2), .q1(shift_register_1_q3[2]), .d2(in_3),
    .q2(shift_register_1_q3[1]), .d3(in_4), .q3(shift_register_1_q3[0]), .d4(in_5),
    .q4(shift_register_1_q7[3]), .d5(in_6), .q5(shift_register_1_q7[2]), .d6(in_7),
    .q6(shift_register_1_q7[1]), .d7(in_8), .q7(shift_register_1_q7[0]));  // open: out
  Hex_Digit_Display hex_digit_display_1 (.value(shift_register_1_q7));  // open: dp
  Hex_Digit_Display hex_digit_display_2 (.value(shift_register_1_q3));  // open: dp
endmodule
